// Logisim project Cache2.circ as structural Verilog: 11 circuits, main circuit main
module main (
  input  EnableTestHalting,
  output [9:0] CorrectCounter,
  output [9:0] HitCounter,
  output [9:0] MissCounter,
  output [9:0] TestNumber,
  output [7:0] ByteRead,
  output [7:0] CorrectByteRead,
  output Halt
);

  wire and_3_out, and_4_out, and_5_out, CLK, CmdIsRead, Correct, CpuRead, CpuWrite, DidContain, HaltTesting,
       MaxItersReached, MemRead, MemWrite, not_1_out, not_2_out, not_4_out, NotDoneTesting, Ok2Count,
       or_1_out, Ready;
  wire [7:0] CpuWriteValue, MemAddress;
  wire [9:0] CpuAddress;
  wire [31:0] Line2Mem, LineFromMem;

  not not_1 (not_1_out, Ready);
  Clock clock_1 (.out(CLK));
  or or_1 (or_1_out, MaxItersReached, Ready);
  Counter #(.width(4), .max('h9)) MaxClocks (
    .load(Ready), .D(4'b0001), .count(not_1_out), .carry(MaxItersReached), .clk(CLK));  // open: Q, clr
  and and_1 (HaltTesting, EnableTestHalting, CmdIsRead, not_2_out);
  not not_2 (not_2_out, Correct);
  not not_3 (NotDoneTesting, Halt);
  Inputs inputs_1 (
    .HaltTesting(HaltTesting), .Ready(or_1_out), .CLK(CLK), .Done(Halt), .Read(CpuRead), .Write(CpuWrite),
    .Address(CpuAddress), .Value(CpuWriteValue), .TestNumber(TestNumber));
  Cache cache_1 (
    .CpuAddress(CpuAddress), .CpuRead(CpuRead), .CpuWrite(CpuWrite), .CpuWriteValue(CpuWriteValue),
    .CLK(CLK), .Ready(Ready), .DidContain(DidContain), .ByteRead(ByteRead), .MemAddress(MemAddress),
    .MemRead(MemRead), .MemWrite(MemWrite), .LineFromMem(LineFromMem), .Line2Mem(Line2Mem));
  // Probe on CpuRead
  // Probe on CpuWrite
  // Probe on CpuAddress
  // Probe on CpuWriteValue
  // Probe on TestNumber
  // Probe on CorrectByteRead
  // Probe on Correct
  // Probe on Ready
  // Probe on DidContain
  // Probe on ByteRead
  // Probe on MemAddress
  // Probe on MemRead
  // Probe on MemWrite
  // Probe on HitCounter
  // Probe on LineFromMem
  // Probe on Line2Mem
  not not_4 (not_4_out, HaltTesting);
  RAM #(.dataWidth(32), .bus("separate")) ram_1 (
    .addr(MemAddress), .din(Line2Mem), .data(LineFromMem), .str(MemWrite), .clk(CLK), .ld(MemRead));  // open: sel, clr
  and and_2 (Ok2Count, Ready, not_4_out, NotDoneTesting);
  and and_3 (and_3_out, Correct, Ok2Count);
  and and_4 (and_4_out, DidContain, Ok2Count);
  and and_5 (and_5_out, MemRead, NotDoneTesting);
  Checker checker_1 (
    .TestNumber(TestNumber), .YourByteRead(ByteRead), .CmdIsRead(CmdIsRead),
    .CorrectByteRead(CorrectByteRead), .Correct(Correct));
  Counter #(.width(10), .max('h3ff)) u_CorrectCounter (
    .count(and_3_out), .Q(CorrectCounter), .clk(CLK));  // open: load, D, carry, clr
  Counter #(.width(10), .max('h3ff)) u_HitCounter (
    .count(and_4_out), .Q(HitCounter), .clk(CLK));  // open: load, D, carry, clr
  Counter #(.width(10), .max('h3ff)) u_MissCounter (
    .count(and_5_out), .Q(MissCounter), .clk(CLK));  // open: load, D, carry, clr
  // Probe on CorrectCounter
  // Probe on HitCounter
  // Probe on MissCounter

  // Other names for the same wires on the sheet: DoneTesting = Halt

  // Notes on the sheet:
  //   Your Answer Inside Here
endmodule

module Cache (
  input  [9:0] CpuAddress,
  input  CpuRead,
  input  CpuWrite,
  input  [7:0] CpuWriteValue,
  input  CLK,
  input  [31:0] LineFromMem,
  output Ready,
  output DidContain,
  output [7:0] ByteRead,
  output [7:0] MemAddress,
  output MemRead,
  output MemWrite,
  output [31:0] Line2Mem
);

  wire ChosenContain, ChosenDirty, CpuReadNow, CPUReadSel, CpuWriteNow, CPUWriteSel, DidContainS1,
       DidContainS2, DirtyS1, DirtyS2, EnableDidContain, SetEnable1, SetEnable2;
  wire [2:0] Next_State, NextStates;
  wire [6:0] WriteAddressS1, WriteAddressS2;
  wire [7:0] BytesS1, BytesS2, WriteOut;
  wire [7:1] AddressW;
  wire [9:0] AddressOut;
  wire [31:0] Line2Mem1, Line2Mem2;

  FSM fsm_1 (
    .Z(Next_State[2]), .Y(Next_State[1]), .X(Next_State[0]), .R(CpuReadNow), .W(CpuWriteNow),
    .C(ChosenContain), .D(ChosenDirty), .ZPrime(NextStates[2]), .YPrime(NextStates[1]), .XPrime(NextStates[0]));
  Register #(.width(3)) StatesReg (.D(NextStates), .Q(Next_State), .clk(CLK));  // open: en, clr
  // Probe on Next_State
  // Probe on NextStates
  Sets sets_1 (
    .CLK(CLK), .SetEnable(SetEnable1), .Read(CpuReadNow), .Write(CpuWriteNow), .State(Next_State),
    .WriteIn(WriteOut), .TAGBITS(WriteAddressS1), .FullLine(Line2Mem1), .ByteRead(BytesS1),
    .DidContain(DidContainS1), .Dirty(DirtyS1), .OFFSET(CpuAddress[1:0]), .TAG(CpuAddress[9:3]),
    .LineFromMem(LineFromMem));
  Comparator #(.width(3), .mode("unsigned")) comparator_1 (.a(Next_State), .b(3'b011), .eq(MemWrite));  // open: gt, lt
  Comparator #(.width(3), .mode("unsigned")) comparator_2 (
    .a(Next_State), .b(3'b010), .eq(EnableDidContain));  // open: gt, lt
  Multiplexer #(.enable("false")) multiplexer_1 (.in0(DirtyS1), .in1(DirtyS2), .out(ChosenDirty), .sel(CpuAddress[2]));
  Register #(.width(10)) CPU_Register (.D(CpuAddress), .en(Ready), .Q(AddressOut), .clk(CLK));  // open: clr
  Multiplexer #(.width(32), .enable("false")) multiplexer_2 (
    .in0(Line2Mem1), .in1(Line2Mem2), .out(Line2Mem), .sel(CpuAddress[2]));
  Register #(.width(1)) u_CPURead (.D(CpuRead), .en(Ready), .Q(CPUReadSel), .clk(CLK));  // open: clr
  Sets sets_2 (
    .CLK(CLK), .SetEnable(SetEnable2), .Read(CpuReadNow), .Write(CpuWriteNow), .State(Next_State),
    .WriteIn(WriteOut), .TAGBITS(WriteAddressS2), .FullLine(Line2Mem2), .ByteRead(BytesS2),
    .DidContain(DidContainS2), .Dirty(DirtyS2), .OFFSET(CpuAddress[1:0]), .TAG(CpuAddress[9:3]),
    .LineFromMem(LineFromMem));
  Multiplexer #(.width(7), .enable("false")) multiplexer_3 (
    .in0(WriteAddressS1), .in1(WriteAddressS2), .out(AddressW), .sel(CpuAddress[2]));
  Multiplexer #(.enable("false")) multiplexer_4 (.in0(CPUReadSel), .in1(CpuRead), .out(CpuReadNow), .sel(Ready));
  Register Write_Register (.D(CpuWriteValue), .en(Ready), .Q(WriteOut), .clk(CLK));  // open: clr
  Register #(.width(1)) u_CPUWrite (.D(CpuWrite), .en(Ready), .Q(CPUWriteSel), .clk(CLK));  // open: clr
  Multiplexer #(.enable("false")) multiplexer_5 (.in0(CPUWriteSel), .in1(CpuWrite), .out(CpuWriteNow), .sel(Ready));
  Multiplexer #(.enable("false")) multiplexer_6 (
    .in0(DidContainS1), .in1(DidContainS2), .out(ChosenContain), .sel(CpuAddress[2]));
  Multiplexer #(.width(8)) multiplexer_7 (
    .in0(BytesS1), .in1(BytesS2), .out(ByteRead), .sel(CpuAddress[2]));  // open: en
  Comparator #(.width(3), .mode("unsigned")) comparator_3 (.a(Next_State), .b(3'b100), .eq(MemRead));  // open: gt, lt
  Decoder decoder_1 (.out0(SetEnable1), .out1(SetEnable2), .sel(CpuAddress[2]));  // open: en
  Multiplexer #(.width(8), .enable("false")) multiplexer_8 (
    .in0(CpuAddress[9:2]), .in1({AddressW, CpuAddress[2]}), .out(MemAddress), .sel(MemWrite));
  Comparator #(.width(3), .mode("unsigned")) comparator_4 (.a(Next_State), .b(3'b001), .eq(Ready));  // open: gt, lt
  Register #(.width(1)) State (.D(ChosenContain), .en(EnableDidContain), .Q(DidContain), .clk(CLK));  // open: clr

  // Other names for the same wires on the sheet: Address[7:0] = CpuAddress[9:2]; TAG[6:0] = CpuAddress[9:3];
  //   AddressW[0] = CpuAddress[2]; SET = CpuAddress[2]; ChooseWrAddress[6:0] = AddressW;
  //   OFFSET[1:0] = CpuAddress[1:0]; EnableWriteAdd = MemWrite; X0 = Next_State[0]; X1 = Next_State[1];
  //   X2 = Next_State[2]

  // Notes on the sheet:
  //   Address Bits = 10
  //   Line Size = 4
  //   W = 3
  //   Num Sets = 2
  //   C =4*3*2 = 24bytes
  //   Tag bits = 7
  //   1
  //   2
endmodule

module Inputs (
  input  HaltTesting,
  input  Ready,
  input  CLK,
  output Done,
  output Read,
  output Write,
  output [9:0] Address,
  output [7:0] Value,
  output [9:0] TestNumber
);

  wire and_1_out, not_1_out, not_2_out;

  not not_1 (not_1_out, HaltTesting);
  not not_2 (not_2_out, Done);
  Counter #(.width(10), .max('h3ff), .ongoal("stay")) u_TestNumber (
    .count(and_1_out), .Q(TestNumber), .clk(CLK));  // open: load, D, carry, clr
  and and_1 (and_1_out, not_1_out, Ready, not_2_out);
  ROM #(.addrWidth(10), .dataWidth(21)) rom_1 (
    .addr(TestNumber), .data({Done, Read, Write, Address, Value}));  // open: sel

  // Notes on the sheet:
  //   contents of rom_1 (hex, n*v repeats v):
  //   80000 80100 80200 80300 80400 80500 80600 80700 80800 80900 80a00 80b00 80c00 80d00 80e00 80f00
  //   81000 81100 81200 81300 81400 81500 81600 81700 0 100000
endmodule

module Checker (
  input  [9:0] TestNumber,
  input  [7:0] YourByteRead,
  output CmdIsRead,
  output [7:0] CorrectByteRead,
  output Correct
);

  wire comparator_1_eq;
  wire [9:0] subtractor_1_out;

  // Probe on TestNumber
  Subtractor #(.width(10)) subtractor_1 (.a(TestNumber), .b(10'h1), .out(subtractor_1_out));  // open: bin, bout
  ROM #(.addrWidth(10), .dataWidth(9)) rom_1 (
    .addr(subtractor_1_out), .data({CmdIsRead, CorrectByteRead}));  // open: sel
  Comparator #(.mode("unsigned")) comparator_1 (
    .a(YourByteRead), .b(CorrectByteRead), .eq(comparator_1_eq));  // open: gt, lt
  and and_1 (Correct, comparator_1_eq, CmdIsRead);

  // Other names for the same wires on the sheet: Test_Number[9:0] = TestNumber

  // Notes on the sheet:
  //   Read Solutions
  //   contents of rom_1 (hex, n*v repeats v):
  //   100 101 102 103 104 105 106 107 108 109 10a 10b 10c 10d 10e 10f 110 111 112 113 114 115 116 117
endmodule

module Sets (
  input  CLK,
  input  SetEnable,
  input  Read,
  input  Write,
  input  [31:0] LineFromMem,
  input  [7:0] WriteIn,
  input  [1:0] OFFSET,
  input  [6:0] TAG,
  input  [2:0] State,
  output [6:0] TAGBITS,
  output Dirty,
  output [31:0] FullLine,
  output [7:0] ByteRead,
  output DidContain
);

  wire and_1_out, and_2_out, and_3_out, and_4_out, and_5_out, and_6_out, and_7_out, and_8_out, and_9_out,
       and_10_out, and_11_out, and_12_out, and_13_out, and_14_out, and_15_out, and_16_out, and_17_out,
       and_18_out, and_19_out, and_20_out, and_21_out, and_22_out, and_23_out, and_24_out, and_25_out,
       and_26_out, and_27_out, and_34_out, comparator_1_eq, comparator_2_eq, comparator_3_eq,
       comparator_5_eq, comparator_6_eq, comparator_7_eq, ContainL1, ContainL2, ContainL3, DidNotContain,
       DirtyL1, DirtyL2, DirtyL3, LE1, LE2, LE3, LineR_W, LineWriteL1_q, LineWriteL2_q, LineWriteL3_q, nCon1,
       nCon2, nCon3, not_1_out, not_2_out, not_3_out, not_4_out, not_5_out, not_6_out, not_7_out, not_8_out,
       not_9_out, not_10_out, not_11_out, not_12_out, not_13_out, not_14_out, not_15_out, not_16_out,
       not_17_out, not_18_out, not_19_out, not_20_out, not_21_out, not_22_out, not_23_out, not_24_out,
       not_25_out, not_26_out, not_27_out, not_28_out, not_29_out, not_30_out, not_31_out, not_32_out,
       not_33_out, not_34_out, not_35_out, not_36_out, not_37_out, not_38_out, not_39_out, not_40_out,
       not_41_out, not_42_out, not_43_out, not_44_out, not_45_out, UpdateAges, UseL1, UseL2, UseL3;
  wire [1:0] InitializeAge1, InitializeAge2, InitializeAge3, NextAge1, NextAge2, NextAge3, SelectLine,
       UPAge1, UPAge2, UPAge3;
  wire [2:0] AllLines, Next_State, NextState;
  wire [6:0] TagL1, TagL2, TagL3;
  wire [7:0] Byte11, Byte12, Byte13, Byte21, Byte22, Byte23, Byte31, Byte32, Byte33, Byte41, Byte42, Byte43,
       ByteReg, multiplexer_2_out, SelByteL1, SelByteL2, SelByteL3;

  // Probe on SelByteL1
  // Probe on SelByteL3
  // Probe on SelByteL2
  not not_1 (not_1_out, State[2]);
  not not_2 (not_2_out, Write);
  not not_3 (not_3_out, Dirty);
  not not_4 (not_4_out, State[2]);
  not not_5 (not_5_out, DidContain);
  not not_6 (not_6_out, Dirty);
  not not_7 (not_7_out, State[2]);
  not not_8 (not_8_out, Read);
  not not_9 (not_9_out, Write);
  not not_10 (not_10_out, State[2]);
  not not_11 (not_11_out, State[2]);
  not not_12 (not_12_out, State[1]);
  not not_13 (not_13_out, State[0]);
  not not_14 (not_14_out, State[1]);
  not not_15 (not_15_out, Read);
  not not_16 (not_16_out, State[1]);
  not not_17 (not_17_out, Dirty);
  not not_18 (not_18_out, State[1]);
  not not_19 (not_19_out, State[2]);
  not not_20 (not_20_out, State[1]);
  not not_21 (not_21_out, Write);
  not not_22 (not_22_out, State[1]);
  not not_23 (not_23_out, Read);
  not not_24 (not_24_out, State[2]);
  not not_25 (not_25_out, State[0]);
  not not_26 (not_26_out, DidContain);
  not not_27 (not_27_out, State[2]);
  not not_28 (not_28_out, State[0]);
  not not_29 (not_29_out, Read);
  not not_30 (not_30_out, State[2]);
  not not_31 (not_31_out, State[0]);
  not not_32 (not_32_out, Write);
  not not_33 (not_33_out, State[1]);
  not not_34 (not_34_out, State[0]);
  not not_35 (not_35_out, State[0]);
  not not_36 (not_36_out, DidContain);
  not not_37 (not_37_out, State[0]);
  not not_38 (not_38_out, Read);
  not not_39 (not_39_out, Write);
  not not_40 (not_40_out, State[0]);
  not not_41 (not_41_out, Dirty);
  not not_42 (not_42_out, State[1]);
  not not_43 (not_43_out, State[0]);
  not not_44 (not_44_out, State[0]);
  not not_45 (not_45_out, Write);
  and and_1 (and_1_out, not_1_out, State[1], not_2_out, not_3_out);
  and and_2 (and_2_out, not_4_out, State[1], not_5_out, not_6_out);
  and and_3 (and_3_out, not_7_out, State[1], not_8_out, not_9_out, DidContain);
  and and_4 (and_4_out, not_10_out, State[1], Read, Write, DidContain);
  and and_5 (and_5_out, not_11_out, State[1], State[0]);
  and and_6 (and_6_out, State[2], not_12_out, not_13_out);
  and and_7 (and_7_out, State[2], not_14_out, not_15_out);
  and and_8 (and_8_out, State[2], not_16_out, Write, not_17_out);
  and and_9 (and_9_out, State[2], not_18_out, Write, DidContain);
  and and_10 (and_10_out, not_19_out, not_20_out, State[0], not_21_out);
  and and_11 (and_11_out, not_22_out, State[0], not_23_out, Write);
  and and_12 (and_12_out, not_24_out, State[1], not_25_out, not_26_out, Dirty);
  and and_13 (and_13_out, not_27_out, State[1], not_28_out, not_29_out, Write, DidContain);
  and and_14 (and_14_out, not_30_out, State[1], not_31_out, Read, not_32_out, Dirty);
  and and_15 (and_15_out, State[2], State[1], State[0], Dirty);
  and and_16 (and_16_out, State[2], State[1], State[0], Write);
  and and_17 (and_17_out, not_33_out, not_34_out);
  and and_18 (and_18_out, not_35_out, not_36_out, Dirty);
  and and_19 (and_19_out, not_37_out, not_38_out, not_39_out, DidContain);
  and and_20 (and_20_out, not_40_out, Read, DidContain, not_41_out);
  and and_21 (and_21_out, not_42_out, Read, Write);
  and and_22 (and_22_out, not_43_out, Read, Write, DidContain);
  and and_23 (and_23_out, State[2], not_44_out);
  and and_24 (and_24_out, State[2], not_45_out);
  and and_25 (and_25_out, State[2], State[1], Dirty);
  and and_26 (and_26_out, State[2], State[1], DidContain);
  // Probe on SelectLine
  or or_1 (NextState[2], and_1_out, and_2_out, and_3_out, and_4_out, and_5_out, and_6_out, and_7_out, and_8_out, and_9_out);
  or or_2 (NextState[1], and_10_out, and_11_out, and_12_out, and_13_out, and_14_out, and_15_out, and_16_out);
  or or_3 (NextState[0], and_17_out, and_18_out, and_19_out, and_20_out, and_21_out, and_22_out, and_23_out, and_24_out, and_25_out, and_26_out);
  Multiplexer #(.select(3), .enable("false")) multiplexer_1 (
    .in0(DirtyL1), .in1(DirtyL1), .in2(DirtyL2), .in3(DirtyL2), .in4(DirtyL3), .in5(DirtyL3), .in6(DirtyL3),
    .in7(DirtyL3), .out(Dirty), .sel(AllLines));
  Multiplexer #(.select(2), .width(8), .enable("false")) multiplexer_2 (
    .in0(SelByteL1), .in1(SelByteL2), .in2(SelByteL3), .out(multiplexer_2_out), .sel(SelectLine));  // open: in3
  // Probe on multiplexer_2_out
  Comparator #(.width(3), .mode("unsigned")) comparator_1 (
    .a(State), .b(3'b101), .eq(comparator_1_eq));  // open: gt, lt
  Lines lines_1 (
    .CLK(CLK), .LineData(LineFromMem), .State(State), .WriteIn(WriteIn), .Contain(ContainL1),
    .Dirty(DirtyL1), .Tag_2(TagL1), .LE(LE1), .OFFSET(OFFSET), .TAG(TAG), .Byte1(Byte11), .Byte2(Byte21),
    .Byte3(Byte31), .Byte4(Byte41));
  Multiplexer #(.select(2), .width(8), .enable("false")) multiplexer_3 (
    .in0(Byte11), .in1(Byte21), .in2(Byte31), .in3(Byte41), .out(SelByteL1), .sel(OFFSET));
  and and_27 (and_27_out, Read, comparator_1_eq);
  // Probe on NextState
  Register #(.width(3)) StatesReg (.D(NextState), .Q(Next_State), .clk(CLK));  // open: en, clr
  // Probe on ByteReg
  Comparator #(.width(2), .mode("unsigned")) comparator_2 (
    .a(2'b10), .b(UPAge1), .eq(comparator_2_eq));  // open: gt, lt
  Register #(.width(2)) Age1 (.D(InitializeAge1), .en(UpdateAges), .Q(UPAge1), .clk(CLK));  // open: clr
  Multiplexer #(.select(2), .width(8), .enable("false")) multiplexer_4 (
    .in0(SelByteL1), .in1(SelByteL2), .in2(SelByteL3), .out(ByteReg), .sel(SelectLine));  // open: in3
  and and_28 (nCon1, comparator_2_eq, DidNotContain);
  and and_29 (LE1, UseL1, SetEnable);
  Register #(.trigger("falling")) u_ByteRead (
    .D(multiplexer_2_out), .en(and_27_out), .Q(ByteRead), .clk(CLK));  // open: clr
  and and_30 (LE2, UseL2, SetEnable);
  Multiplexer #(.select(2), .width(8), .enable("false")) multiplexer_5 (
    .in0(Byte12), .in1(Byte22), .in2(Byte32), .in3(Byte42), .out(SelByteL2), .sel(OFFSET));
  and and_31 (LE3, UseL3, SetEnable);
  Register #(.width(2)) Age2 (.D(InitializeAge2), .en(UpdateAges), .Q(UPAge2), .clk(CLK));  // open: clr
  Lines lines_2 (
    .CLK(CLK), .LineData(LineFromMem), .State(State), .WriteIn(WriteIn), .Contain(ContainL2),
    .Dirty(DirtyL2), .Tag_2(TagL2), .LE(LE2), .OFFSET(OFFSET), .TAG(TAG), .Byte1(Byte12), .Byte2(Byte22),
    .Byte3(Byte32), .Byte4(Byte42));
  or or_4 (UpdateAges, comparator_5_eq, and_34_out);
  Comparator #(.width(2), .mode("unsigned")) comparator_3 (
    .a(2'b10), .b(UPAge2), .eq(comparator_3_eq));  // open: gt, lt
  and and_32 (nCon2, comparator_3_eq, DidNotContain);
  Ages ages_1 (
    .Age1(UPAge1), .Age2(UPAge2), .Age3(UPAge3), .SelAge(SelectLine), .NextAge1(NextAge1),
    .NextAge2(NextAge2), .NextAge3(NextAge3));
  Comparator #(.width(3), .mode("unsigned")) comparator_4 (.a(3'b010), .b(State), .eq(LineR_W));  // open: gt, lt
  Register #(.width(2)) Age3 (.D(InitializeAge3), .en(UpdateAges), .Q(UPAge3), .clk(CLK));  // open: clr
  Multiplexer #(.select(2), .width(7), .enable("false")) multiplexer_6 (
    .in0(TagL1), .in1(TagL2), .in2(TagL3), .out(TAGBITS), .sel(SelectLine));  // open: in3
  Multiplexer #(.select(2), .width(8), .enable("false")) multiplexer_7 (
    .in0(Byte13), .in1(Byte23), .in2(Byte33), .in3(Byte43), .out(SelByteL3), .sel(OFFSET));
  // Probe on OFFSET
  // Probe on Byte33
  // Probe on Byte43
  Comparator #(.width(3), .mode("unsigned")) comparator_5 (
    .a(State), .b(3'b000), .eq(comparator_5_eq));  // open: gt, lt
  Multiplexer #(.select(3), .width(2), .enable("false")) multiplexer_8 (
    .in0(2'b01), .in1(NextAge2), .in2(NextAge2), .in3(NextAge2), .in4(NextAge2), .in5(NextAge2),
    .in6(NextAge2), .in7(NextAge2), .out(InitializeAge2), .sel(State));
  // Probe on Byte13
  // Probe on Byte23
  Comparator #(.width(2), .mode("unsigned")) comparator_6 (
    .a(2'b10), .b(UPAge3), .eq(comparator_6_eq));  // open: gt, lt
  and and_33 (nCon3, comparator_6_eq, DidNotContain);
  Multiplexer #(.select(3), .width(2), .enable("false")) multiplexer_9 (
    .in0(2'b00), .in1(NextAge1), .in2(NextAge1), .in3(NextAge1), .in4(NextAge1), .in5(NextAge1),
    .in6(NextAge1), .in7(NextAge1), .out(InitializeAge1), .sel(State));
  Comparator #(.width(3), .mode("unsigned")) comparator_7 (
    .a(State), .b(3'b101), .eq(comparator_7_eq));  // open: gt, lt
  // Probe on AllLines[0]
  and and_34 (and_34_out, SetEnable, comparator_7_eq);
  Lines lines_3 (
    .CLK(CLK), .LineData(LineFromMem), .State(State), .WriteIn(WriteIn), .Contain(ContainL3),
    .Dirty(DirtyL3), .Tag_2(TagL3), .LE(LE3), .OFFSET(OFFSET), .TAG(TAG), .Byte1(Byte13), .Byte2(Byte23),
    .Byte3(Byte33), .Byte4(Byte43));
  Multiplexer #(.select(3), .width(2), .enable("false")) multiplexer_10 (
    .in0(2'b10), .in1(NextAge3), .in2(NextAge3), .in3(NextAge3), .in4(NextAge3), .in5(NextAge3),
    .in6(NextAge3), .in7(NextAge3), .out(InitializeAge3), .sel(State));
  or or_5 (AllLines[0], ContainL1, nCon1);
  // Probe on AllLines[1]
  or or_6 (AllLines[1], ContainL2, nCon2);
  // Probe on AllLines[2]
  or or_7 (DidContain, ContainL1, ContainL2, ContainL3);
  not not_46 (DidNotContain, DidContain);
  Multiplexer #(.select(2), .width(32), .enable("false")) multiplexer_11 (
    .in0({Byte41, Byte31, Byte21, Byte11}), .in1({Byte42, Byte32, Byte22, Byte12}),
    .in2({Byte43, Byte33, Byte23, Byte13}), .out(FullLine), .sel(SelectLine));  // open: in3
  or or_8 (AllLines[2], ContainL3, nCon3);
  Register #(.width(1)) LineWriteL1 (.D(AllLines[0]), .en(LineR_W), .Q(LineWriteL1_q), .clk(CLK));  // open: clr
  Multiplexer #(.select(3), .enable("false")) multiplexer_12 (
    .in0(AllLines[0]), .in1(AllLines[0]), .in2(AllLines[0]), .in3(LineWriteL1_q), .in4(LineWriteL1_q),
    .in5(LineWriteL1_q), .in6(LineWriteL1_q), .in7(LineWriteL1_q), .out(UseL1), .sel(State));
  Register #(.width(1)) LineWriteL2 (.D(AllLines[1]), .en(LineR_W), .Q(LineWriteL2_q), .clk(CLK));  // open: clr
  Multiplexer #(.select(3), .width(2), .enable("false")) multiplexer_13 (
    .in0(2'b00), .in1(2'b00), .in2(2'b01), .in4(2'b10), .out(SelectLine), .sel({LE3, LE2, LE1}));  // open: in3, in5, in6, in7
  Multiplexer #(.select(3), .enable("false")) multiplexer_14 (
    .in0(AllLines[1]), .in1(AllLines[1]), .in2(AllLines[1]), .in3(LineWriteL2_q), .in4(LineWriteL2_q),
    .in5(LineWriteL2_q), .in6(LineWriteL2_q), .in7(LineWriteL2_q), .out(UseL2), .sel(State));
  // Probe on SelectLine
  Register #(.width(1)) LineWriteL3 (.D(AllLines[2]), .en(LineR_W), .Q(LineWriteL3_q), .clk(CLK));  // open: clr
  Multiplexer #(.select(3), .enable("false")) multiplexer_15 (
    .in0(AllLines[2]), .in1(AllLines[2]), .in2(AllLines[2]), .in3(LineWriteL3_q), .in4(LineWriteL3_q),
    .in5(LineWriteL3_q), .in6(LineWriteL3_q), .in7(LineWriteL3_q), .out(UseL3), .sel(State));

  // Other names for the same wires on the sheet: DirtyLine[2:0] = AllLines; LineWriteL1 = AllLines[0];
  //   LineWriteL2 = AllLines[1]; LineWriteL3 = AllLines[2]; Line1[31:0] = {Byte41, Byte31, Byte21, Byte11};
  //   Line2[31:0] = {Byte42, Byte32, Byte22, Byte12}; Line3[31:0] = {Byte43, Byte33, Byte23, Byte13};
  //   ReadEnable = Read; X0 = State[0]; X1 = State[1]; X2 = State[2]; WriteEnable = Write
endmodule

module Lines (
  input  CLK,
  input  [31:0] LineData,
  input  LE,
  input  [1:0] OFFSET,
  input  [6:0] TAG,
  input  [2:0] State,
  input  [7:0] WriteIn,
  output [7:0] Byte1,
  output [7:0] Byte2,
  output [7:0] Byte3,
  output [7:0] Byte4,
  output [6:0] Tag_2,
  output Dirty,
  output Contain
);

  wire and_1_out, comparator_1_eq, comparator_2_eq, comparator_3_eq, comparator_4_eq, comparator_5_eq,
       comparator_6_eq, comparator_7_eq, comparator_8_eq, comparator_9_eq, comparator_10_eq,
       comparator_11_eq, comparator_12_eq, comparator_17_eq, DirtyEnable, InDirty, InDirtys, not_1_out,
       or_1_out, Valid;
  wire [0:0] multiplexer_6_out;
  wire [1:0] bitselector_1_out;
  wire [6:0] testTag;
  wire [7:0] ByteIn1, ByteIn2, ByteIn3, ByteIn4, ByteIn16, ByteIn26, ByteIn36, ByteIn46, ByteOut1, ByteOut2,
       ByteOut3, ByteOut4, multiplexer_5_out, multiplexer_7_out, multiplexer_9_out, multiplexer_10_out,
       RegIN1, RegIN2, RegIN3, RegIN4;
  wire [31:0] LineSize_q;

  Comparator #(.width(3), .mode("unsigned")) comparator_1 (
    .a(State), .b(3'b100), .eq(comparator_1_eq));  // open: gt, lt
  Comparator #(.width(3), .mode("unsigned")) comparator_2 (
    .a(State), .b(3'b110), .eq(comparator_2_eq));  // open: gt, lt
  Register #(.width(32)) LineSize (.D(LineData), .Q(LineSize_q), .clk(CLK));  // open: en, clr
  // Probe on LineSize_q
  Multiplexer #(.width(8), .enable("false")) multiplexer_1 (
    .in1(LineData[15:8]), .out(ByteIn2), .sel(comparator_1_eq));  // open: in0
  Multiplexer #(.width(8), .enable("false")) multiplexer_2 (
    .in1(ByteOut2), .out(ByteIn26), .sel(comparator_2_eq));  // open: in0
  Comparator #(.width(3), .mode("unsigned")) comparator_3 (
    .a(State), .b(3'b100), .eq(comparator_3_eq));  // open: gt, lt
  Comparator #(.width(3), .mode("unsigned")) comparator_4 (
    .a(State), .b(3'b110), .eq(comparator_4_eq));  // open: gt, lt
  Comparator #(.width(3), .mode("unsigned")) comparator_5 (
    .a(State), .b(3'b100), .eq(comparator_5_eq));  // open: gt, lt
  Multiplexer #(.width(8), .enable("false")) multiplexer_3 (
    .in1(LineData[7:0]), .out(ByteIn1), .sel(comparator_3_eq));  // open: in0
  Multiplexer #(.width(8), .enable("false")) multiplexer_4 (
    .in1(ByteOut1), .out(ByteIn16), .sel(comparator_4_eq));  // open: in0
  and and_1 (and_1_out, comparator_5_eq, LE);
  Multiplexer #(.select(3), .width(8), .enable("false")) multiplexer_5 (
    .in4(ByteIn2), .in6(ByteIn26), .out(multiplexer_5_out), .sel(State));  // open: in0, in1, in2, in3, in5, in7
  Comparator #(.width(3), .mode("unsigned")) comparator_6 (
    .a(State), .b(3'b100), .eq(comparator_6_eq));  // open: gt, lt
  Multiplexer #(.select(2), .width(8), .enable("false")) multiplexer_6 (
    .in0(LineData[7:0]), .in1(LineData[15:8]), .in2(LineData[23:16]), .in3(LineData[31:24]),
    .out({testTag, multiplexer_6_out[0]}), .sel(OFFSET));
  Multiplexer #(.select(3), .width(8), .enable("false")) multiplexer_7 (
    .in4(ByteIn1), .in6(ByteIn16), .out(multiplexer_7_out), .sel(State));  // open: in0, in1, in2, in3, in5, in7
  Register #(.width(7)) u_Tag (.D(TAG), .en(and_1_out), .Q(Tag_2), .clk(CLK));  // open: clr
  Comparator #(.width(3), .mode("unsigned")) comparator_7 (
    .a(State), .b(3'b100), .eq(comparator_7_eq));  // open: gt, lt
  or or_1 (or_1_out, comparator_7_eq, comparator_8_eq);
  Comparator #(.width(3), .mode("unsigned")) comparator_8 (
    .a(State), .b(3'b110), .eq(comparator_8_eq));  // open: gt, lt
  not not_1 (not_1_out, comparator_6_eq);
  Multiplexer #(.enable("false")) multiplexer_8 (.in0(1'b0), .in1(1'b1), .out(InDirty), .sel(not_1_out));
  // Probe on testTag
  Multiplexer #(.select(3), .width(8), .enable("false")) multiplexer_9 (
    .in4(ByteIn4), .in6(ByteIn46), .out(multiplexer_9_out), .sel(State));  // open: in0, in1, in2, in3, in5, in7
  and and_2 (DirtyEnable, or_1_out, LE);
  Register #(.width(1)) u_Dirty (.D(InDirty), .en(DirtyEnable), .Q(Dirty), .clk(CLK));  // open: clr
  Multiplexer #(.select(3), .width(8), .enable("false")) multiplexer_10 (
    .in4(ByteIn3), .in6(ByteIn36), .out(multiplexer_10_out), .sel(State));  // open: in0, in1, in2, in3, in5, in7
  Register #(.width(1)) u_Valid (.D(1'b1), .en(and_1_out), .Q(Valid), .clk(and_1_out));  // open: clr
  Comparator #(.width(3), .mode("unsigned")) comparator_9 (
    .a(State), .b(3'b100), .eq(comparator_9_eq));  // open: gt, lt
  Comparator #(.width(3), .mode("unsigned")) comparator_10 (
    .a(State), .b(3'b110), .eq(comparator_10_eq));  // open: gt, lt
  Comparator #(.width(3), .mode("unsigned")) comparator_11 (
    .a(State), .b(3'b100), .eq(comparator_11_eq));  // open: gt, lt
  Comparator #(.width(3), .mode("unsigned")) comparator_12 (
    .a(State), .b(3'b110), .eq(comparator_12_eq));  // open: gt, lt
  // Probe on bitselector_1_out
  BitSelector #(.width(2), .group(2)) bitselector_1 (.in(OFFSET), .out(bitselector_1_out), .sel(1'b1));
  Multiplexer #(.width(8), .enable("false")) multiplexer_11 (
    .in1(LineData[23:16]), .out(ByteIn3), .sel(comparator_9_eq));  // open: in0
  Multiplexer #(.width(8), .enable("false")) multiplexer_12 (
    .in1(ByteOut3), .out(ByteIn36), .sel(comparator_10_eq));  // open: in0
  Multiplexer #(.width(8), .enable("false")) multiplexer_13 (
    .in1(LineData[31:24]), .out(ByteIn4), .sel(comparator_11_eq));  // open: in0
  Multiplexer #(.width(8), .enable("false")) multiplexer_14 (
    .in1(ByteOut4), .out(ByteIn46), .sel(comparator_12_eq));  // open: in0
  // OR_Gate or_2 has open pins: in0=ByteIn1, in1=ByteIn16, out=open
  Comparator #(.width(2), .mode("unsigned")) comparator_13 (.a(OFFSET), .b(2'b00));  // open: gt, eq, lt
  Comparator #(.width(2), .mode("unsigned")) comparator_14 (.a(OFFSET), .b(2'b01));  // open: gt, eq, lt
  Comparator #(.width(2), .mode("unsigned")) comparator_15 (.a(OFFSET), .b(2'b10));  // open: gt, eq, lt
  Comparator #(.width(2), .mode("unsigned")) comparator_16 (.a(OFFSET), .b(2'b11));  // open: gt, eq, lt
  Multiplexer #(.select(3), .enable("false")) multiplexer_15 (
    .in0(1'b1), .in1(1'b1), .in2(1'b1), .in3(1'b1), .in4(1'b0), .in5(1'b1), .in6(1'b1), .in7(1'b1),
    .out(InDirtys), .sel(State));
  // Probe on LineData[7:0]
  // Probe on LineData[15:8]
  // Probe on LineData[23:16]
  // Probe on LineData[31:24]
  // OR_Gate or_3 has open pins: in0=ByteIn2, in1=ByteIn26, out=open
  Register u_Byte1 (.D(RegIN1), .en(DirtyEnable), .Q(Byte1), .clk(CLK));  // open: clr
  // OR_Gate or_4 has open pins: in0=ByteIn3, in1=ByteIn36, out=open
  Register u_Byte2 (.D(RegIN2), .en(DirtyEnable), .Q(Byte2), .clk(CLK));  // open: clr
  Multiplexer #(.select(3), .width(8), .enable("false")) multiplexer_16 (
    .in4(LineData[7:0]), .in6(ByteOut1), .out(RegIN1), .sel(State));  // open: in0, in1, in2, in3, in5, in7
  Multiplexer #(.select(3), .width(8), .enable("false")) multiplexer_17 (
    .in4(LineData[15:8]), .in6(ByteOut2), .out(RegIN2), .sel(State));  // open: in0, in1, in2, in3, in5, in7
  Multiplexer #(.select(3), .width(8), .enable("false")) multiplexer_18 (
    .in4(LineData[23:16]), .in6(ByteOut3), .out(RegIN3), .sel(State));  // open: in0, in1, in2, in3, in5, in7
  Multiplexer #(.select(3), .width(8), .enable("false")) multiplexer_19 (
    .in4(LineData[31:24]), .in6(ByteOut4), .out(RegIN4), .sel(State));  // open: in0, in1, in2, in3, in5, in7
  // Probe on RegIN4
  Register u_Byte3 (.D(RegIN3), .en(DirtyEnable), .Q(Byte3), .clk(CLK));  // open: clr
  // Probe on RegIN1
  // Probe on RegIN2
  // Probe on RegIN3
  // OR_Gate or_5 has open pins: in0=ByteIn4, in1=ByteIn46, out=open
  Register u_Byte4 (.D(RegIN4), .en(DirtyEnable), .Q(Byte4), .clk(CLK));  // open: clr
  Multiplexer #(.select(2), .width(8), .enable("false")) multiplexer_20 (
    .in0(WriteIn), .in1(Byte1), .in2(Byte1), .in3(Byte1), .out(ByteOut1), .sel(OFFSET));
  Comparator #(.width(7), .mode("unsigned")) comparator_17 (.a(Tag_2), .b(TAG), .eq(comparator_17_eq));  // open: gt, lt
  // Probe on ByteOut1
  Multiplexer #(.select(2), .width(8), .enable("false")) multiplexer_21 (
    .in0(Byte2), .in1(WriteIn), .in2(Byte2), .in3(Byte2), .out(ByteOut2), .sel(OFFSET));
  and and_3 (Contain, comparator_17_eq, Valid);
  Multiplexer #(.select(2), .width(8), .enable("false")) multiplexer_22 (
    .in0(Byte3), .in1(Byte3), .in2(WriteIn), .in3(Byte3), .out(ByteOut3), .sel(OFFSET));
  Multiplexer #(.select(2), .width(8), .enable("false")) multiplexer_23 (
    .in0(Byte4), .in1(Byte4), .in2(Byte4), .in3(WriteIn), .out(ByteOut4), .sel(OFFSET));

  // Other names for the same wires on the sheet: Byte1Sav[7:0] = Byte1; Byte2Sav[7:0] = Byte2; Byte3Sav[7:0] = Byte3;
  //   Byte4Sav[7:0] = Byte4; CpuTag[6:0] = Tag_2; Byte1_t[7:0] = LineData[7:0]; Byte2_t[7:0] = LineData[15:8];
  //   Byte3_t[7:0] = LineData[23:16]; Byte4_t[7:0] = LineData[31:24]; LineEnable = LE
endmodule

module Ages (
  input  [1:0] Age1,
  input  [1:0] Age2,
  input  [1:0] Age3,
  input  [1:0] SelAge,
  output [1:0] NextAge1,
  output [1:0] NextAge2,
  output [1:0] NextAge3
);

  wire [1:0] Sum, Sum2, Sum3;
  wire [2:0] comparator_3_gt, comparator_6_gt, comparator_9_gt;

  Comparator #(.width(2), .mode("unsigned")) comparator_1 (
    .a(Age1), .b(SelAge), .eq(comparator_3_gt[2]));  // open: gt, lt
  Comparator #(.width(2), .mode("unsigned")) comparator_2 (
    .a(Age1), .b(SelAge), .lt(comparator_3_gt[1]));  // open: gt, eq
  Comparator #(.width(2), .mode("unsigned")) comparator_3 (
    .a(Age1), .b(SelAge), .gt(comparator_3_gt[0]));  // open: eq, lt
  Adder #(.width(2)) adder_1 (.a(Age1), .b(2'b01), .out(Sum));  // open: cin, cout
  // Probe on Sum
  Multiplexer #(.select(3), .width(2), .enable("false")) multiplexer_1 (
    .in1(2'b00), .in2(Sum), .in4(Age1), .out(NextAge1), .sel(comparator_3_gt));  // open: in0, in3, in5, in6, in7
  // Probe on NextAge1
  Comparator #(.width(2), .mode("unsigned")) comparator_4 (
    .a(Age2), .b(SelAge), .eq(comparator_6_gt[2]));  // open: gt, lt
  Comparator #(.width(2), .mode("unsigned")) comparator_5 (
    .a(Age2), .b(SelAge), .lt(comparator_6_gt[1]));  // open: gt, eq
  Comparator #(.width(2), .mode("unsigned")) comparator_6 (
    .a(Age2), .b(SelAge), .gt(comparator_6_gt[0]));  // open: eq, lt
  Adder #(.width(2)) adder_2 (.a(Age2), .b(2'b01), .out(Sum2));  // open: cin, cout
  Multiplexer #(.select(3), .width(2), .enable("false")) multiplexer_2 (
    .in1(2'b00), .in2(Sum2), .in4(Age2), .out(NextAge2), .sel(comparator_6_gt));  // open: in0, in3, in5, in6, in7
  Comparator #(.width(2), .mode("unsigned")) comparator_7 (
    .a(Age3), .b(SelAge), .eq(comparator_9_gt[2]));  // open: gt, lt
  Comparator #(.width(2), .mode("unsigned")) comparator_8 (
    .a(Age3), .b(SelAge), .lt(comparator_9_gt[1]));  // open: gt, eq
  Adder #(.width(2)) adder_3 (.a(Age3), .b(2'b01), .out(Sum3));  // open: cin, cout
  Comparator #(.width(2), .mode("unsigned")) comparator_9 (
    .a(Age3), .b(SelAge), .gt(comparator_9_gt[0]));  // open: eq, lt
  Multiplexer #(.select(3), .width(2), .enable("false")) multiplexer_3 (
    .in1(2'b00), .in2(Sum3), .in4(Age3), .out(NextAge3), .sel(comparator_9_gt));  // open: in0, in3, in5, in6, in7
endmodule

module FSM (
  input  Z,
  input  Y,
  input  X,
  input  R,
  input  W,
  input  C,
  input  D,
  output ZPrime,
  output YPrime,
  output XPrime
);

  wire and_1_out, and_2_out, and_3_out, and_4_out, and_5_out, and_6_out, and_7_out, and_8_out, and_9_out,
       and_10_out, and_11_out, and_12_out, and_13_out, and_14_out, and_15_out, and_16_out, and_17_out,
       and_18_out, and_19_out, and_20_out, and_21_out, and_22_out, and_23_out, and_24_out, and_25_out,
       and_26_out, not_1_out, not_2_out, not_3_out, not_4_out, not_5_out, not_6_out, not_7_out, not_8_out,
       not_9_out, not_10_out, not_11_out, not_12_out, not_13_out, not_14_out, not_15_out, not_16_out,
       not_17_out, not_18_out, not_19_out, not_20_out, not_21_out, not_22_out, not_23_out, not_24_out,
       not_25_out, not_26_out, not_27_out, not_28_out, not_29_out, not_30_out, not_31_out, not_32_out,
       not_33_out, not_34_out, not_35_out, not_36_out, not_37_out, not_38_out, not_39_out, not_40_out,
       not_41_out, not_42_out, not_43_out, not_44_out, not_45_out;

  not not_1 (not_1_out, Z);
  not not_2 (not_2_out, W);
  not not_3 (not_3_out, D);
  not not_4 (not_4_out, Z);
  not not_5 (not_5_out, C);
  not not_6 (not_6_out, D);
  not not_7 (not_7_out, Z);
  not not_8 (not_8_out, R);
  not not_9 (not_9_out, W);
  not not_10 (not_10_out, Z);
  not not_11 (not_11_out, Z);
  not not_12 (not_12_out, Y);
  not not_13 (not_13_out, X);
  not not_14 (not_14_out, Y);
  not not_15 (not_15_out, R);
  not not_16 (not_16_out, Y);
  not not_17 (not_17_out, D);
  not not_18 (not_18_out, Y);
  not not_19 (not_19_out, Z);
  not not_20 (not_20_out, Y);
  not not_21 (not_21_out, W);
  not not_22 (not_22_out, Y);
  not not_23 (not_23_out, R);
  not not_24 (not_24_out, Z);
  not not_25 (not_25_out, X);
  not not_26 (not_26_out, C);
  not not_27 (not_27_out, Z);
  not not_28 (not_28_out, X);
  not not_29 (not_29_out, R);
  not not_30 (not_30_out, Z);
  not not_31 (not_31_out, X);
  not not_32 (not_32_out, W);
  not not_33 (not_33_out, Y);
  not not_34 (not_34_out, X);
  not not_35 (not_35_out, X);
  not not_36 (not_36_out, C);
  not not_37 (not_37_out, X);
  not not_38 (not_38_out, R);
  not not_39 (not_39_out, W);
  not not_40 (not_40_out, X);
  not not_41 (not_41_out, D);
  not not_42 (not_42_out, Y);
  not not_43 (not_43_out, X);
  not not_44 (not_44_out, X);
  not not_45 (not_45_out, W);
  and and_1 (and_1_out, not_1_out, Y, not_2_out, not_3_out);
  and and_2 (and_2_out, not_4_out, Y, not_5_out, not_6_out);
  and and_3 (and_3_out, not_7_out, Y, not_8_out, not_9_out, C);
  and and_4 (and_4_out, not_10_out, Y, R, W, C);
  and and_5 (and_5_out, not_11_out, Y, X);
  and and_6 (and_6_out, Z, not_12_out, not_13_out);
  and and_7 (and_7_out, Z, not_14_out, not_15_out);
  and and_8 (and_8_out, Z, not_16_out, W, not_17_out);
  and and_9 (and_9_out, Z, not_18_out, W, C);
  and and_10 (and_10_out, not_19_out, not_20_out, X, not_21_out);
  and and_11 (and_11_out, not_22_out, X, not_23_out, W);
  and and_12 (and_12_out, not_24_out, Y, not_25_out, not_26_out, D);
  and and_13 (and_13_out, not_27_out, Y, not_28_out, not_29_out, W, C);
  and and_14 (and_14_out, not_30_out, Y, not_31_out, R, not_32_out, D);
  and and_15 (and_15_out, Z, Y, X, D);
  and and_16 (and_16_out, Z, Y, X, W);
  and and_17 (and_17_out, not_33_out, not_34_out);
  and and_18 (and_18_out, not_35_out, not_36_out, D);
  and and_19 (and_19_out, not_37_out, not_38_out, not_39_out, C);
  and and_20 (and_20_out, not_40_out, R, C, not_41_out);
  and and_21 (and_21_out, not_42_out, R, W);
  and and_22 (and_22_out, not_43_out, R, W, C);
  and and_23 (and_23_out, Z, not_44_out);
  and and_24 (and_24_out, Z, not_45_out);
  and and_25 (and_25_out, Z, Y, D);
  and and_26 (and_26_out, Z, Y, C);
  or or_1 (ZPrime, and_1_out, and_2_out, and_3_out, and_4_out, and_5_out, and_6_out, and_7_out, and_8_out, and_9_out);
  or or_2 (YPrime, and_10_out, and_11_out, and_12_out, and_13_out, and_14_out, and_15_out, and_16_out);
  or or_3 (XPrime, and_17_out, and_18_out, and_19_out, and_20_out, and_21_out, and_22_out, and_23_out, and_24_out, and_25_out, and_26_out);
endmodule

module NextState (
  input  CLK,
  input  Z,
  input  Y,
  input  X,
  input  R,
  input  W,
  input  C,
  input  D,
  output [2:0] NextState
);

  wire and_1_out, and_2_out, and_3_out, and_4_out, and_5_out, and_6_out, and_7_out, and_8_out, and_9_out,
       and_10_out, and_11_out, and_12_out, and_13_out, and_14_out, and_15_out, and_16_out, not_1_out,
       not_2_out, not_3_out, not_4_out, not_5_out, not_6_out, not_7_out, not_8_out, not_9_out, not_10_out,
       not_11_out, not_12_out, not_13_out, not_14_out, not_15_out, not_16_out, not_17_out, not_18_out,
       not_19_out, not_20_out, not_21_out, not_22_out, not_23_out;
  wire [2:0] Next_State, State;

  not not_1 (not_1_out, Z);
  not not_2 (not_2_out, D);
  not not_3 (not_3_out, Z);
  not not_4 (not_4_out, X);
  not not_5 (not_5_out, R);
  not not_6 (not_6_out, W);
  not not_7 (not_7_out, Y);
  not not_8 (not_8_out, R);
  not not_9 (not_9_out, X);
  not not_10 (not_10_out, R);
  not not_11 (not_11_out, C);
  not not_12 (not_12_out, D);
  not not_13 (not_13_out, C);
  not not_14 (not_14_out, Z);
  not not_15 (not_15_out, C);
  not not_16 (not_16_out, Z);
  not not_17 (not_17_out, Z);
  not not_18 (not_18_out, Y);
  not not_19 (not_19_out, X);
  not not_20 (not_20_out, Y);
  not not_21 (not_21_out, R);
  not not_22 (not_22_out, W);
  not not_23 (not_23_out, W);
  and and_1 (and_1_out, not_1_out, Y, not_2_out);
  and and_2 (and_2_out, not_3_out, Y, not_4_out, not_5_out, not_6_out, C);
  and and_3 (and_3_out, Z, not_7_out, not_8_out);
  and and_4 (and_4_out, Z, not_9_out, not_10_out, W, not_11_out, not_12_out);
  and and_5 (and_5_out, X, not_13_out, D);
  and and_6 (and_6_out, X, W);
  and and_7 (and_7_out, not_14_out, X, R);
  and and_8 (and_8_out, Y, not_15_out, D);
  and and_9 (and_9_out, Y, W);
  and and_10 (and_10_out, not_16_out, Y, R);
  and and_11 (and_11_out, Y, X, D);
  and and_12 (and_12_out, Z, D);
  and and_13 (and_13_out, Z, W);
  and and_14 (and_14_out, not_17_out, not_18_out, not_19_out);
  and and_15 (and_15_out, not_20_out, not_21_out, not_22_out);
  and and_16 (and_16_out, Z, not_23_out);
  or or_1 (State[2], and_1_out, and_2_out, and_3_out, and_4_out);
  or or_2 (State[1], and_5_out, and_6_out, and_7_out, and_8_out, and_9_out, and_10_out, and_11_out, and_12_out, and_13_out);
  or or_3 (State[0], and_14_out, and_15_out, D, C, and_16_out);
  // Probe on State
  // Probe on {Z, Y, X}
  Multiplexer #(.select(3), .width(3), .enable("false")) multiplexer_1 (
    .in0(Next_State), .in1(Next_State), .in2(Next_State), .in3(Next_State), .in4(Next_State),
    .in5(Next_State), .in6(Next_State), .in7(3'b111), .out(NextState), .sel({Z, Y, X}));
  // Probe on NextState
  Register #(.width(3)) States (.D(State), .Q(Next_State), .clk(CLK));  // open: en, clr

  // Other names for the same wires on the sheet: CurrState[2:0] = {Z, Y, X}; X0 = X; X1 = Y; X2 = Z
endmodule

module EnableRegs (
  input  x2,
  input  x1,
  input  x0,
  input  LE,
  output TE,
  output DE,
  output VE
);

  wire not_1_out, not_2_out, not_3_out, not_4_out, not_5_out;

  not not_1 (not_1_out, x1);
  not not_2 (not_2_out, x0);
  not not_3 (not_3_out, x0);
  not not_4 (not_4_out, x1);
  not not_5 (not_5_out, x0);
  and and_1 (TE, x2, not_1_out, not_2_out, LE);
  and and_2 (DE, x2, x1, not_3_out, LE);
  and and_3 (VE, x2, not_4_out, not_5_out, LE);
endmodule

module LineFSMControl (
  input  LE3,
  input  LE2,
  input  LE1,
  output B1,
  output B0
);

  wire not_1_out, not_2_out, not_3_out, not_4_out;

  not not_1 (not_1_out, LE2);
  not not_2 (not_2_out, LE1);
  not not_3 (not_3_out, LE3);
  not not_4 (not_4_out, LE1);
  and and_1 (B1, LE3, not_1_out, not_2_out);
  and and_2 (B0, not_3_out, LE2, not_4_out);

  // Other names for the same wires on the sheet: LineControl[2:0] = {LE3, LE2, LE1}
endmodule
